# Fritzing sketch Scheme (saved by Fritzing 0.9.4)
perfboards: 1

parts:
  LCD1 = LCD screen
  J3 = Camdenboss CTB0158-2 [part_number=CTB0158-2 package=THT]
  S1 = Momentary Switch [package=ksa_sealed_tac_switch]
  S2 = Momentary Switch [package=ksa_sealed_tac_switch]
  S3 = Momentary Switch [package=ksa_sealed_tac_switch]
  S4 = Momentary Switch [package=ksa_sealed_tac_switch]
  Componente2 = Arduino Micro (Rev3)
  R1 = Resistor [tolerance=±5% resistance=10k package=THT]
  R2 = Resistor [tolerance=±5% resistance=10k package=THT]  # not connected
  R3 = Resistor [tolerance=±5% resistance=10k package=THT]
  R4 = Resistor [tolerance=±5% resistance=10k package=THT]
  LCM1602_IIC1 = LCM1602 IIC [part_number="LCM1602 IIC" chip_label="LCM1602 IIC" package="DIP (Dual Inline) [THT]"]
  M1 = RioRand LM2596
  WeMos_D1_Mini_Relay_Shield_V1 = WeMos D1 Mini Relay Shield V2
  J1 = Camdenboss CTB0158-3 [part_number=CTB0158-3 package=THT]

nets:
  N1: LCD1.VSS, LCM1602_IIC1.K
  N2: LCD1.VDD, LCM1602_IIC1.A
  N3: LCD1.V0, LCM1602_IIC1.D7
  N4: LCD1.RS, LCM1602_IIC1.D6
  N5: LCD1.R/W, LCM1602_IIC1.D5
  N6: LCD1.E, LCM1602_IIC1.D4
  N7: LCD1.DB0, LCM1602_IIC1.D3
  N8: LCD1.DB1, LCM1602_IIC1.D2
  N9: LCD1.DB2, LCM1602_IIC1.D1
  N10: LCD1.DB3, LCM1602_IIC1.D0
  N11: LCD1.DB4, LCM1602_IIC1.E
  N12: LCD1.DB5, LCM1602_IIC1.RW
  N13: LCD1.DB6, LCM1602_IIC1.RS
  N14: LCD1.DB7, LCM1602_IIC1.V0
  N15: LCD1.LED+, LCM1602_IIC1.VDD
  N16: LCD1.LED-, LCM1602_IIC1.VSS
  N17: J3.pin1, M1.Pin_1
  N18: J3.pin2, M1.Pin_2
  N19: S1.1, Componente2.D6_PWM/A7, R1.Pin_1
  N20: S1.4, S2.4, S3.4, S4.4
  N21: S2.1, Componente2.D7, R3.Pin_1
  N22: S3.1, Componente2.D5_PWM, R4.Pin_1
  5V: S3.3, Componente2.5V, LCM1602_IIC1.VCC, J1.pin1
  N23: S4.1, Componente2.D8_PWM/A8
  GND: Componente2.GND, R4.Pin_0, LCM1602_IIC1.GND, M1.Pin_4, WeMos_D1_Mini_Relay_Shield_V1.G, J1.pin3
  N24: Componente2.D2/SDA, LCM1602_IIC1.SDA
  N25: Componente2.D3/SCL, LCM1602_IIC1.SCL
  N26: Componente2.D10_PWM/A10, WeMos_D1_Mini_Relay_Shield_V1.D1
  VIN: Componente2.VIN, M1.Pin_3, WeMos_D1_Mini_Relay_Shield_V1.5V
  N27: Componente2.A5, J1.pin2
  N28: R1.Pin_0, R3.Pin_0
  N29: LCM1602_IIC1.LED_A, LCM1602_IIC1.LED_B

custom parts:
  LCM1602 IIC: I2C-Module to use a 1602 or 2004 LCD on with the wire.h libory Serial LCD Modul
